# Fritzing sketch Coral_TeachableMachine_MagPi (saved by Fritzing 0.9.3b)
breadboards: 1

parts:
  Raspberry_Pi_1 = Raspberry Pi 3 [part_number=RPI-3-V1.2]
  S5 = Momentary Switch [package=ksa_sealed_tac_switch]
  R1 = Resistor [tolerance=±5% resistance=330 package=THT]
  S6 = Momentary Switch [package=ksa_sealed_tac_switch]
  R2 = Resistor [tolerance=±5% resistance=330 package=THT]
  S7 = Momentary Switch [package=ksa_sealed_tac_switch]
  S8 = Momentary Switch [package=ksa_sealed_tac_switch]
  R3 = Resistor [tolerance=±5% resistance=330 package=THT]
  R4 = Resistor [tolerance=±5% resistance=330 package=THT]
  S9 = Momentary Switch [package=ksa_sealed_tac_switch]
  LED6 = smd LED [color="Red (633nm)" package="1206 [SMD]"]
  LED7 = smd LED [color="Orange (620nm)" package="1206 [SMD]"]
  LED8 = smd LED [color="Green (555nm)" package="1206 [SMD]"]
  LED9 = smd LED [color="Blue (430nm)" package="1206 [SMD]"]

nets:
  N1: Raspberry_Pi_1.3v3, S5.2, S6.2, S7.2, S8.2, S9.2
  N2: Raspberry_Pi_1.GIPO5, S9.4
  N3: Raspberry_Pi_1.GIPO6, S8.4
  N4: Raspberry_Pi_1.GIPO13, S7.4
  N5: Raspberry_Pi_1.GIPO19, S6.4
  N6: Raspberry_Pi_1.GIPO26, S5.4
  N7: Raspberry_Pi_1.GIPO21, R1.Pin_0
  N8: Raspberry_Pi_1.GIPO20, R2.Pin_0
  N9: Raspberry_Pi_1.GIPO16, R3.Pin_0
  N10: Raspberry_Pi_1.GIPO12, R4.Pin_0
  N11: S5.1, LED9.anode
  N12: R1.Pin_1, LED9.cathode
  N13: S6.1, LED8.anode
  N14: R2.Pin_1, LED8.cathode
  N15: S7.1, LED7.anode
  N16: S8.1, LED6.anode
  N17: R3.Pin_1, LED7.cathode
  N18: R4.Pin_1, LED6.cathode
